// Logisim project universal_gates_nand_nor.circ as structural Verilog: 1 circuit, main circuit main
module main (
  input  a,
  input  b,
  output a_prime,
  output a_NAND_b,
  output a_prime_2,
  output a_NAND_b_2,
  output a_prime_3,
  output n_ab,
  output a_AND_b,
  output ab,
  output a_NOR_b,
  output ab_2,
  output n_a_b,
  output a_OR_b,
  output a_NOR_b_2,
  output a_b,
  output a_b_2
);

  wire nand_2_out, nand_3_out, nand_4_out, nand_9_out, nand_10_out, nand_11_out, nor_2_out, nor_3_out,
       nor_4_out, nor_7_out, nor_8_out, nor_9_out, not_1_out, not_2_out;

  not not_1 (not_1_out, b);
  not not_2 (not_2_out, a);
  not not_3 (a_prime, a);
  nand nand_1 (a_prime_2, a, a);
  nor nor_1 (a_prime_3, a, a);
  and and_1 (a_AND_b, a, b);
  nand nand_2 (nand_2_out, a, b);
  nor nor_2 (nor_2_out, a, a);
  nor nor_3 (nor_3_out, b, b);
  or or_1 (a_OR_b, a, b);
  nand nand_3 (nand_3_out, a, a);
  nand nand_4 (nand_4_out, b, b);
  nor nor_4 (nor_4_out, a, b);
  nand nand_5 (ab, nand_2_out, nand_2_out);
  nor nor_5 (ab_2, nor_2_out, nor_3_out);
  nand nand_6 (a_b, nand_3_out, nand_4_out);
  nor nor_6 (a_b_2, nor_4_out, nor_4_out);
  nand nand_7 (a_NAND_b, b, a);
  nand nand_8 (a_NAND_b_2, b, a);
  nor nor_7 (nor_7_out, b, b);
  nor nor_8 (nor_8_out, nor_7_out, nor_9_out);
  nor nor_9 (nor_9_out, a, a);
  nor nor_10 (a_NOR_b, b, a);
  nand nand_9 (nand_9_out, b, b);
  nand nand_10 (nand_10_out, nand_9_out, nand_11_out);
  nand nand_11 (nand_11_out, a, a);
  nor nor_11 (a_NOR_b_2, a, b);
  nor nor_12 (n_ab, nor_8_out, nor_8_out);
  nand nand_12 (n_a_b, nand_10_out, nand_10_out);

  // Notes on the sheet:
  //   a
  //   a
  //   a
  //   a
  //   b
  //   a
  //   b
  //   a
  //   b
  //   a
  //   b
  //   a
  //   b
  //   a
  //   b
  //   !(ab)
  //   a'
  //   b'
  //   a'
  //   b'
  //   !(a+b)
  //   NOT a
  //   NOT a
  //   ab
  //   a+b
  //   NOT a
  //   a AND b
  //   a AND b
  //   a OR b
  //   a OR b
  //   b
  //   a
  //   b
  //   a
  //   b
  //   a
  //   b
  //   a
  //   b
  //   a
  //   b
  //   a
  //   !(ab)
  //   !(ab)
  //   b'
  //   ab
  //   a'
  //   !(a+b)
  //   b'
  //   a+b
  //   a'
  //   !(a+b)
  //   a NAND b
  //   a NOR b
endmodule
